# Fritzing sketch ir (saved by Fritzing 0.8.7b)
circuit board: 8.46667cm x 5.64444cm
breadboards: 1

parts:
  IR1 = TSOP312.., 314.. [package=THT]
  Part1 = Arduino Uno (Rev3) - ICSP
  LED1 = LED - 3mm [color="Red (633nm)" package="3 mm [THT]"]
  LED2 = LED - 3mm [color="Yellow (585nm)" package="3 mm [THT]"]
  LED3 = LED - 3mm [color="Green (570nm)" package="3 mm [THT]"]
  LED4 = LED - 3mm [color="Blue (525nm)" package="3 mm [THT]"]
  R1 = Resistor [tolerance=±5% resistance=1k package=THT]
  R2 = Resistor [tolerance=±5% resistance=1k package=THT]
  R3 = Resistor [tolerance=±5% resistance=1k package=THT]
  R4 = Resistor [tolerance=±5% resistance=1k package=THT]
  R4_2 = Resistor [tolerance=±5% resistance=220 package=THT]

nets (from the breadboard view):
  GND: IR1.GND, Part1.GND, LED1.cathode, LED2.cathode, LED3.cathode, LED4.cathode
  N1: IR1.Vs, Part1.5V
  N2: IR1.Data, Part1.D13/SCK
  N3: Part1.D8, R1.Pin_1
  N4: Part1.D9_PWM, R2.Pin_1
  N5: Part1.D10_PWM/SS, R3.Pin_1
  N6: Part1.D11_PWM/MOSI, R4.Pin_1, R4_2.Pin_1
  N7: LED1.anode, R1.Pin_0
  N8: LED2.anode, R2.Pin_0
  N9: LED3.anode, R3.Pin_0
  N10: LED4.anode, R4.Pin_0, R4_2.Pin_0

// code stored in the sketch: IR rec decoder.ino
#include <IRremote.h> // By MMKaresz

int RECV_PIN = 11;
int ONE = 2;
int TWO = 3;
int THREE = 4;
int FOUR = 5;
int pwm = 0 ;
int ONEval = 2;
int TWOval = 2;
int THREEval = 2;
int FOURval= 2;
IRrecv irrecv(RECV_PIN);

decode_results results;

void setup() {
  Serial.begin(9600);
  irrecv.enableIRIn(); // Start the receiver
  pinMode(ONE, OUTPUT);
  pinMode(TWO, OUTPUT);
  pinMode(THREE, OUTPUT);
  pinMode(FOUR, OUTPUT);
  digitalWrite(ONE, LOW);
  digitalWrite(TWO, LOW);
  digitalWrite(THREE, LOW);
  analogWrite(FOUR, 0);
}

void loop() {
  if (irrecv.decode(&results)) {
    Serial.println(results.value);  // Shows the IR remote code in the serial monitor
      switch (results.value){

    case 3249166758:          // btn 1
      Serial.print("ONE - "); 
      Serial.println(ONEval);
      ONEval=ONEval+1;			//counts up, switch on if its even number
      if (ONEval % 2) { digitalWrite(ONE,HIGH); }				// if its even number...
      if ( (ONEval & 0x01) == 0) { digitalWrite(ONE,LOW); }		//if its odd number...
      delay(200);
    break;
      
    case 3249147378:          //btn 2
    Serial.print("TWO - ");
    Serial.println(TWOval);
      TWOval=TWOval+1;
      if (TWOval % 2) { digitalWrite(TWO,HIGH); }				// if its even number...
      if ( (TWOval & 0x01) == 0) { digitalWrite(TWO,LOW); }		//if its odd number...
      delay(200);
    break;
   
    case 3249152478:          //btn 3
      Serial.print("THREE - ");
      Serial.println(THREEval);
      THREEval=THREEval+1;
      if (THREEval % 2) { digitalWrite(THREE,HIGH); }       	// if its even number...
      if ( (THREEval & 0x01) == 0) { digitalWrite(THREE,LOW); } //if its odd number...
      delay(200);
      break;

    case 3249180018:         // vol up
      Serial.print("up - ");    
    	pwm=pwm+5;
    	if (pwm>=255){
    		pwm=255;
    	}
    	analogWrite(FOUR,pwm);  
    	Serial.println(pwm);
      break;
    
    case 3249196338:        // vol down
      Serial.print("down - ");    
	   	pwm=pwm-5;
    	if (pwm<=0){
    		pwm=0;
    	}
    	analogWrite(FOUR,pwm);  
      	Serial.println(pwm);
      break;
      
    case 3249195318:       // 1-2-3 off
      Serial.println("OFF");    
      digitalWrite(ONE,LOW);
      digitalWrite(TWO,LOW);
      digitalWrite(THREE,LOW);
      ONEval = 2;
      TWOval = 2;
      THREEval = 2;
      break;
 }
  delay(20);
  if (ONEval==5) { ONEval=1;}
  if (TWOval==5) { TWOval=1;}
  if (THREEval==5) { THREEval=1;}
  irrecv.resume(); // Receive the next value
  }
}
