# Fritzing sketch lcd (saved by Fritzing 0.8.7b)
breadboards: 1

parts:
  Part1 = Arduino Uno (Rev3)
  U1 = LCD-16X2 [package=lcd-16x2]
  R1 = Rotary Potentiometer (Large) [maximum_resistance=100kΩ package=THT]
  S1 = Pushbutton [package="[THT]"]
  R2 = Resistor [tolerance=±5% resistance=10k package=THT]

nets:
  N1: Part1.D8, U1.E
  N2: Part1.D9_PWM, U1.DB4
  N3: Part1.D10_PWM/SS, U1.DB5
  N4: Part1.D11_PWM/MOSI, U1.DB6
  N5: Part1.D12/MISO, U1.DB7
  N6: Part1.D2, S1.Pin_3, S1.Pin_4, R2.Pin_1
  N7: Part1.D7, U1.RS
  5V: Part1.5V, U1.VDD, U1.A, R1.leg1, R2.Pin_0
  GND: Part1.GND, U1.VSS, U1.R_W, U1.K, R1.leg2, S1.Pin_1, S1.Pin_2
  N8: U1.VO, R1.wiper
