# Fritzing sketch car (saved by Fritzing 0.8.7b)

parts:
  Part1 = Arduino Uno (Rev3)  # not connected
  Mod1 = Arduino Sensor Shield v5.0
  VCC1 = 4 x AAA Battery Mount
  S1 = H-Bridge with L298N
  M1 = DC Motor
  M3 = DC Motor
  M4 = DC Motor
  M2 = DC Motor
  J1 = Basic Servo
  Part2 = SRF05 Ultrasonic Rangefinder
  LED1 = smd LED [color="Blue (525nm)" package="1206 [SMD]"]
  LED1_2 = smd LED [color="Blue (525nm)" package="1206 [SMD]"]
  R1 = Resistor [tolerance=±5% resistance=220 package=THT]
  R3 = Resistor [tolerance=±5% resistance=220 package=THT]

nets:
  VCC: Mod1.VCC, Mod1.COM-VCC, Mod1.AREF-V, Mod1.11-V, Mod1.0-V, VCC1.+, S1.12V, S1.ENB-5V, J1.vcc, Part2.VCC
  N1: Mod1.SD-D13, Mod1.13-S, Part2.Trig
  GND: Mod1.GND, Mod1.IIC-GND, Mod1.BLUETOOTH-GND, Mod1.AREF-G, Mod1.11-G, Mod1.10-G, Mod1.9-G, VCC1.-, S1.GND, J1.gnd, Part2.GND, R1.Pin_0, R3.Pin_0
  N2: Mod1.12-S, Part2.Echo
  N3: Mod1.11-S, J1.pulse
  N4: Mod1.10-S, Mod1.ParallelLCD-D10, LED1_2.cathode
  N5: Mod1.9-S, Mod1.ParallelLCD-D9, LED1.cathode
  N6: Mod1.7-S, S1.IN1
  N7: Mod1.6-S, S1.ENA
  N8: Mod1.5-S, S1.IN2
  N9: Mod1.4-S, S1.IN3
  N10: Mod1.3-S, S1.ENB
  N11: Mod1.2-S, S1.IN4
  N12: S1.M1-01, M1.pin_2, M2.pin_2
  N13: S1.M1-02, M1.pin_1, M2.pin_1
  N14: S1.M2-01, M3.pin_1, M4.pin_1
  N15: S1.M2-02, M3.pin_2, M4.pin_2

custom parts:
  Arduino Sensor Shield v5.0: Arduino Sensor Shield v5.0 provides I2C interface, Bluetooth module communication interface, SD card module communication interface, APC220 wireless RF modules communication interface, RB URF V1.1 ultrasonic sensors interface, 12864 LCD serial and parallel interface, 32 servo controller interfaces. In addition (with the sel jumper removed) allows an external power supply for the servos as the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
  H-Bridge with L298N: h-bridge
